// Logisim project 0509 i forgo.circ as structural Verilog: 1 circuit, main circuit main
module main (
  input  A,
  input  B,
  input  C
);

  // AND_Gate S0 has open pins: in0=A, in1=B, in2=C, out=open
  // AND_Gate S1 has open pins: in0=A, in1=B, in2=C, out=open
  // AND_Gate S2 has open pins: in0=A, in1=B, in2=C, out=open
  // AND_Gate S3 has open pins: in0=A, in1=B, in2=C, out=open
  // AND_Gate S4 has open pins: in0=A, in1=B, in2=C, out=open
  // AND_Gate S5 has open pins: in0=A, in1=B, in2=C, out=open
  // AND_Gate S6 has open pins: in0=A, in1=B, in2=C, out=open
  // AND_Gate S7 has open pins: in0=A, in1=B, in2=C, out=open
endmodule
