// Logisim project 3 contadores.circ as structural Verilog: 4 circuits, main circuit main
module main (
);

  wire [2:0] \contador_síncrono_com_flip_flop_jk_1_out_3 ;
  wire [3:0] \contador_assíncrono_com_flip_flop_jk_1_out_4 ;
  wire [4:0] contador_up_com_flip_flop_jk_1_out_5;

  Contador_Up_com_Flip_Flop_JK contador_up_com_flip_flop_jk_1 (
    .out_1(contador_up_com_flip_flop_jk_1_out_5[4]), .out_2(contador_up_com_flip_flop_jk_1_out_5[3]),
    .out_3(contador_up_com_flip_flop_jk_1_out_5[2]), .out_4(contador_up_com_flip_flop_jk_1_out_5[1]),
    .out_5(contador_up_com_flip_flop_jk_1_out_5[0]));
  // Probe on contador_up_com_flip_flop_jk_1_out_5
  \Contador_Assíncrono_com_Flip_Flop_JK  \contador_assíncrono_com_flip_flop_jk_1  (
    .out_1(\contador_assíncrono_com_flip_flop_jk_1_out_4 [3]),
    .out_2(\contador_assíncrono_com_flip_flop_jk_1_out_4 [2]),
    .out_3(\contador_assíncrono_com_flip_flop_jk_1_out_4 [1]),
    .out_4(\contador_assíncrono_com_flip_flop_jk_1_out_4 [0]));
  // Probe on \contador_assíncrono_com_flip_flop_jk_1_out_4 
  \Contador_Síncrono_com_Flip_Flop_JK  \contador_síncrono_com_flip_flop_jk_1  (
    .out_1(\contador_síncrono_com_flip_flop_jk_1_out_3 [2]),
    .out_3(\contador_síncrono_com_flip_flop_jk_1_out_3 [0]),
    .out_2(\contador_síncrono_com_flip_flop_jk_1_out_3 [1]));
  // Probe on \contador_síncrono_com_flip_flop_jk_1_out_3 
  // Probe on \contador_síncrono_com_flip_flop_jk_1_out_3 
endmodule

module \Contador_Assíncrono_com_Flip_Flop_JK  (
  output out_1,
  output out_2,
  output out_3,
  output out_4
);

  wire clock_1_out;

  Clock clock_1 (.out(clock_1_out));
  J_K_Flip_Flop j_k_ff_1 (.J(1'b1), .clk(clock_1_out), .K(1'b1), .Q(out_4));  // open: Qn, preset, en, reset
  // Probe on {out_1, out_2, out_3, out_4}
  J_K_Flip_Flop j_k_ff_2 (.J(1'b1), .clk(out_4), .K(1'b1), .Q(out_3));  // open: Qn, preset, en, reset
  J_K_Flip_Flop j_k_ff_3 (.J(1'b1), .clk(out_3), .K(1'b1), .Q(out_2));  // open: Qn, preset, en, reset
  J_K_Flip_Flop j_k_ff_4 (.J(1'b1), .clk(out_2), .K(1'b1), .Q(out_1));  // open: Qn, preset, en, reset
endmodule

module Contador_Up_com_Flip_Flop_JK (
  output out_1,
  output out_2,
  output out_3,
  output out_4,
  output out_5
);

  wire clock_1_out, j_k_ff_1_qn, j_k_ff_2_qn, j_k_ff_3_qn, j_k_ff_4_qn;

  Clock clock_1 (.out(clock_1_out));
  J_K_Flip_Flop j_k_ff_1 (
    .J(1'b1), .clk(clock_1_out), .K(1'b1), .Q(out_5), .Qn(j_k_ff_1_qn));  // open: preset, en, reset
  J_K_Flip_Flop j_k_ff_2 (
    .J(1'b1), .clk(j_k_ff_1_qn), .K(1'b1), .Q(out_4), .Qn(j_k_ff_2_qn));  // open: preset, en, reset
  // Probe on {out_1, out_2, out_3, out_4, out_5}
  J_K_Flip_Flop j_k_ff_3 (
    .J(1'b1), .clk(j_k_ff_2_qn), .K(1'b1), .Q(out_3), .Qn(j_k_ff_3_qn));  // open: preset, en, reset
  J_K_Flip_Flop j_k_ff_4 (
    .J(1'b1), .clk(j_k_ff_3_qn), .K(1'b1), .Q(out_2), .Qn(j_k_ff_4_qn));  // open: preset, en, reset
  J_K_Flip_Flop j_k_ff_5 (.J(1'b1), .clk(j_k_ff_4_qn), .K(1'b1), .Q(out_1));  // open: Qn, preset, en, reset
endmodule

module \Contador_Síncrono_com_Flip_Flop_JK  (
  output out_1,
  output out_2,
  output out_3
);

  wire and_1_out, clock_1_out, or_1_out, or_2_out;

  Clock clock_1 (.out(clock_1_out));
  and and_1 (and_1_out, ~out_3, out_2);  // AND_Gate
  or or_1 (or_1_out, out_1, ~out_3);  // OR_Gate
  J_K_Flip_Flop j_k_ff_1 (.J(and_1_out), .clk(clock_1_out), .K(and_1_out), .Q(out_1));  // open: Qn, preset, en, reset
  J_K_Flip_Flop j_k_ff_2 (.J(or_1_out), .clk(clock_1_out), .K(or_1_out), .Q(out_2));  // open: Qn, preset, en, reset
  // Probe on {out_1, out_2, out_3}
  or or_2 (or_2_out, ~out_1, out_2);  // OR_Gate
  J_K_Flip_Flop j_k_ff_3 (.J(or_2_out), .clk(clock_1_out), .K(or_2_out), .Q(out_3));  // open: Qn, preset, en, reset
  // Probe on {out_1, out_2, out_3}
endmodule
