// Logisim project 7seg vowels.circ as structural Verilog: 2 circuits, main circuit main
module main (
  input  in_1,
  input  in_2,
  input  in_3,
  input  in_4
);

  wire clock_1_out, vowels_1_a_2, vowels_1_b_2, vowels_1_c_2, vowels_1_d, vowels_1_e, vowels_1_f, vowels_1_g,
       vowels_2_a_2, vowels_2_b_2, vowels_2_c_2, vowels_2_d, vowels_2_e, vowels_2_f, vowels_2_g;
  wire [2:0] counter_1_q;

  vowels vowels_1 (
    .a_2(vowels_1_a_2), .b_2(vowels_1_b_2), .c_2(vowels_1_c_2), .d(vowels_1_d), .e(vowels_1_e),
    .f(vowels_1_f), .g(vowels_1_g), .A(in_1), .B(in_2), .C(in_3));
  _7_Segment_Display u_7_segment_display_1 (
    .g(in_4), .f(in_4), .a(in_4), .b(in_4), .e(in_4), .d(in_4), .c(in_4));  // open: dp
  _7_Segment_Display u_7_segment_display_2 (
    .g(vowels_1_g), .f(vowels_1_f), .a(vowels_1_a_2), .b(vowels_1_b_2), .e(vowels_1_e), .d(vowels_1_d),
    .c(vowels_1_c_2));  // open: dp
  Clock clock_1 (.out(clock_1_out));
  Counter #(.width(3), .max('h7)) counter_1 (.Q(counter_1_q), .clk(clock_1_out));  // open: load, D, count, carry, clr
  vowels vowels_2 (
    .a_2(vowels_2_a_2), .b_2(vowels_2_b_2), .c_2(vowels_2_c_2), .d(vowels_2_d), .e(vowels_2_e),
    .f(vowels_2_f), .g(vowels_2_g), .A(counter_1_q[2]), .B(counter_1_q[1]), .C(counter_1_q[0]));
  _7_Segment_Display u_7_segment_display_3 (
    .g(vowels_2_g), .f(vowels_2_f), .a(vowels_2_a_2), .b(vowels_2_b_2), .e(vowels_2_e), .d(vowels_2_d),
    .c(vowels_2_c_2));  // open: dp
endmodule

module vowels (
  input  A,
  input  B,
  input  C,
  output a_2,
  output b_2,
  output c_2,
  output d,
  output e,
  output f,
  output g
);

  and and_1 (g, ~A, ~B);  // AND_Gate
  or or_1 (b_2, B, ~C);  // OR_Gate
  or or_2 (d, A, C);
  or or_3 (e, C, ~B);  // OR_Gate
  or or_4 (a_2, g, C);

  assign c_2 = b_2;
  assign f = e;
endmodule
