// Logisim project exemplo1.circ as structural Verilog: 4 circuits, main circuit main
module main (
  input  [3:0] in_1,
  input  [3:0] in_2,
  input  in_3,
  output out_4,
  output [3:0] out_5
);

  Soma_4bits soma_4bits_1 (.A(in_2), .B(in_1), .Soma(out_5), .Overflow(out_4), .in_3(in_3));
endmodule

module Add1 (
  input  A,
  input  B,
  input  Vem_1,
  output S,
  output Vai_1
);

  wire and_1_out, and_2_out, and_3_out, xor_1_out;

  xor xor_1 (xor_1_out, A, B);
  and and_1 (and_1_out, A, Vem_1);
  and and_2 (and_2_out, A, B);
  and and_3 (and_3_out, B, Vem_1);
  xor xor_2 (S, xor_1_out, Vem_1);
  or or_1 (Vai_1, and_1_out, and_2_out, and_3_out);
endmodule

module Soma_4bits (
  input  [3:0] B,
  input  [3:0] A,
  input  in_3,
  output Overflow,
  output [3:0] Soma
);

  wire add1_2_vai_1, add1_3_vai_1, add1_4_vai_1;

  // Probe on B
  Add1 add1_1 (.A(B[3]), .B(A[3]), .Vem_1(add1_2_vai_1), .S(Soma[3]), .Vai_1(Overflow));
  Add1 add1_2 (.A(B[2]), .B(A[2]), .Vem_1(add1_4_vai_1), .S(Soma[2]), .Vai_1(add1_2_vai_1));
  // Probe on Soma
  Add1 add1_3 (.A(B[0]), .B(A[0]), .Vem_1(in_3), .S(Soma[0]), .Vai_1(add1_3_vai_1));
  Add1 add1_4 (.A(B[1]), .B(A[1]), .Vem_1(add1_3_vai_1), .S(Soma[1]), .Vai_1(add1_4_vai_1));
  // Probe on A
endmodule

module exemplo1 (
  input  A,
  input  B,
  input  C,
  output S
);

  wire not_1_out, not_2_out, or_1_out, xor_1_out;

  not not_1 (not_1_out, A);
  xor xor_1 (xor_1_out, A, B);
  not not_2 (not_2_out, C);
  or or_1 (or_1_out, xor_1_out, not_1_out);
  and and_1 (S, or_1_out, not_2_out);
endmodule
