// Logisim project exemplo2.circ as structural Verilog: 3 circuits, main circuit exemplo1
module main (
  input  A,
  input  B,
  input  C,
  input  A_2,
  input  B_2,
  input  C_2,
  output S,
  output S_2
);

  exemplo1 exemplo1_1 (.A(A), .B(B), .C(C), .S(S));
  exemplo2 exemplo2_1 (.A(A_2), .B(B_2), .C(C_2), .out_4(S_2));
endmodule

module exemplo1 (
  input  A,
  input  B,
  input  C,
  output S
);

  wire not_1_out, or_1_out, xor_1_out;

  xor xor_1 (xor_1_out, A, B);
  not not_1 (not_1_out, C);
  or or_1 (or_1_out, xor_1_out, ~A);  // OR_Gate
  and and_1 (S, or_1_out, not_1_out);
endmodule

module exemplo2 (
  input  A,
  input  B,
  input  C,
  output out_4
);

  wire and_1_out, or_1_out, xor_1_out;

  xor xor_1 (xor_1_out, A, B);
  or or_1 (or_1_out, xor_1_out, ~B);  // OR_Gate
  and and_1 (and_1_out, or_1_out, ~A);  // AND_Gate
  or or_2 (out_4, and_1_out, ~C);  // OR_Gate
endmodule
