// Logisim project relogio xdd.circ as structural Verilog
module relogio (
  output [3:0] out_1,
  output [3:0] out_2,
  output [3:0] out_3,
  output [3:0] out_4,
  output [3:0] out_5,
  output [3:0] out_6
);

  wire and_1_out, and_2_out, and_3_out, and_4_out, and_5_out, and_6_out, and_7_out, and_8_out, clock_1_out,
       or_1_out;

  and and_1 (and_1_out, and_3_out, and_2_out);
  Counter #(.width(4), .max('hf)) counter_1 (
    .Q(out_1), .clk(or_1_out), .clr(and_1_out));  // open: load, D, count, carry
  and and_2 (and_2_out, ~out_2[3], out_2[2], ~out_2[1], ~out_2[0]);  // AND_Gate
  Counter #(.width(4), .max('hf)) counter_2 (
    .Q(out_2), .clk(and_5_out), .clr(or_1_out));  // open: load, D, count, carry
  and and_3 (and_3_out, ~out_1[3], ~out_1[2], out_1[1], ~out_1[0]);  // AND_Gate
  and and_4 (and_4_out, out_2[3], ~out_2[2], out_2[1], ~out_2[0]);  // AND_Gate
  or or_1 (or_1_out, and_2_out, and_4_out);
  Counter #(.width(4), .max('hf)) counter_3 (
    .Q(out_3), .clk(and_6_out), .clr(and_5_out));  // open: load, D, count, carry
  and and_5 (and_5_out, ~out_3[3], out_3[2], out_3[1], ~out_3[0]);  // AND_Gate
  Counter #(.width(4), .max('hf)) counter_4 (
    .Q(out_4), .clk(and_7_out), .clr(and_6_out));  // open: load, D, count, carry
  and and_6 (and_6_out, out_4[3], ~out_4[2], out_4[1], ~out_4[0]);  // AND_Gate
  Counter #(.width(4), .max('hf)) counter_5 (
    .Q(out_5), .clk(and_8_out), .clr(and_7_out));  // open: load, D, count, carry
  and and_7 (and_7_out, ~out_5[3], out_5[2], out_5[1], ~out_5[0]);  // AND_Gate
  Counter #(.width(4), .max('hf)) counter_6 (
    .Q(out_6), .clk(clock_1_out), .clr(and_8_out));  // open: load, D, count, carry
  Clock clock_1 (.out(clock_1_out));
  and and_8 (and_8_out, out_6[3], ~out_6[2], out_6[1], ~out_6[0]);  // AND_Gate
endmodule
