// Logisim project sub1.circ as structural Verilog: 2 circuits, main circuit main
module main (
  input  A,
  input  B,
  input  C,
  output V,
  output S
);

  sub_1 sub_1_1 (.S(S), .V(V), .A(A), .B(B), .C(C));
endmodule

module sub_1 (
  input  A,
  input  B,
  input  C,
  output S,
  output V
);

  wire and_1_out, and_2_out, or_1_out, xor_1_out;

  xor xor_1 (xor_1_out, A, B);
  or or_1 (or_1_out, B, C);
  and and_1 (and_1_out, B, C);
  and and_2 (and_2_out, or_1_out, ~A);  // AND_Gate
  xor xor_2 (S, xor_1_out, C);
  or or_2 (V, and_2_out, and_1_out);
endmodule
