// Logisim project display7.circ as structural Verilog: 2 circuits, main circuit main
module main (
  input  in_1,
  input  in_2,
  input  in_3,
  input  in_4
);

  wire display7_1_a_2, display7_1_b_2, display7_1_out_7, display7_1_out_8, display7_1_out_9,
       display7_1_out_10, display7_1_out_11;

  display7 display7_1 (
    .a_2(display7_1_a_2), .b_2(display7_1_b_2), .out_7(display7_1_out_7), .out_8(display7_1_out_8),
    .out_9(display7_1_out_9), .out_10(display7_1_out_10), .out_11(display7_1_out_11), .A(in_1), .B(in_2),
    .C(in_3), .D(in_4));
  _7_Segment_Display u_7_segment_display_1 (
    .g(display7_1_out_11), .f(display7_1_out_10), .a(display7_1_a_2), .b(display7_1_b_2),
    .e(display7_1_out_9), .d(display7_1_out_8), .c(display7_1_out_7));  // open: dp
endmodule

module display7 (
  input  A,
  input  B,
  input  C,
  input  D,
  output a_2,
  output b_2,
  output out_7,
  output out_8,
  output out_9,
  output out_10,
  output out_11
);

  wire and_1_out, and_2_out, and_3_out, and_4_out, and_5_out, and_6_out, and_7_out, and_8_out, and_9_out,
       and_10_out, and_11_out, and_12_out, xor_1_out, xor_2_out;

  xor xor_1 (xor_1_out, B, D);
  xor xor_2 (xor_2_out, C, D);
  and and_1 (and_1_out, ~B, ~D);  // AND_Gate
  and and_2 (and_2_out, ~B, C);  // AND_Gate
  and and_3 (and_3_out, C, ~D);  // AND_Gate
  and and_4 (and_4_out, B, ~C, D);  // AND_Gate
  and and_5 (and_5_out, ~B, ~D);  // AND_Gate
  and and_6 (and_6_out, C, ~D);  // AND_Gate
  and and_7 (and_7_out, ~C, ~D);  // AND_Gate
  and and_8 (and_8_out, B, ~C);  // AND_Gate
  and and_9 (and_9_out, B, ~D);  // AND_Gate
  and and_10 (and_10_out, B, ~C);  // AND_Gate
  and and_11 (and_11_out, ~B, C);  // AND_Gate
  and and_12 (and_12_out, C, ~D);  // AND_Gate
  or or_1 (a_2, A, C, ~xor_1_out);  // OR_Gate
  or or_2 (b_2, ~B, ~xor_2_out);  // OR_Gate
  or or_3 (out_7, B, ~C, D);  // OR_Gate
  or or_4 (out_9, and_5_out, and_6_out);
  or or_5 (out_8, A, and_1_out, and_2_out, and_3_out, and_4_out);
  or or_6 (out_10, A, and_7_out, and_8_out, and_9_out);
  or or_7 (out_11, A, and_10_out, and_11_out, and_12_out);
endmodule
