// Logisim project sub4_bits.circ as structural Verilog: 3 circuits, main circuit main
module main (
  input  A,
  input  B,
  input  C,
  output V,
  output S
);

  sub_1 sub_1_1 (.S(S), .V(V), .A(A), .B(B), .C(C));
endmodule

module sub_1 (
  input  A,
  input  B,
  input  C,
  output S,
  output V
);

  wire and_1_out, and_2_out, or_1_out, xor_1_out;

  xor xor_1 (xor_1_out, A, B);
  or or_1 (or_1_out, B, C);
  and and_1 (and_1_out, B, C);
  and and_2 (and_2_out, or_1_out, ~A);  // AND_Gate
  xor xor_2 (S, xor_1_out, C);
  or or_2 (V, and_2_out, and_1_out);
endmodule

module Sub_4bits (
  input  [3:0] B,
  input  [3:0] A,
  input  in_3,
  output Overflow,
  output [3:0] Subtracao
);

  wire sub_1_2_v, sub_1_3_v, sub_1_4_v;

  // Probe on B
  sub_1 sub_1_1 (.S(Subtracao[3]), .V(Overflow), .A(A[3]), .B(B[3]), .C(sub_1_2_v));
  sub_1 sub_1_2 (.S(Subtracao[2]), .V(sub_1_2_v), .A(A[2]), .B(B[2]), .C(sub_1_3_v));
  // Probe on Subtracao
  sub_1 sub_1_3 (.S(Subtracao[1]), .V(sub_1_3_v), .A(A[1]), .B(B[1]), .C(sub_1_4_v));
  sub_1 sub_1_4 (.S(Subtracao[0]), .V(sub_1_4_v), .A(A[0]), .B(B[0]), .C(in_3));
  // Probe on A
endmodule
